# Fritzing sketch neje_vertical (saved by Fritzing 0.9.2b)
circuit board: 7.99625cm x 4.69636cm
breadboards: 4

parts:
  ULN2003A = ULN2003A [package="DIP16 [THT]"]
  +5V_LSR = female pin header, 2 pins [form="♀ (female)"]
  57ohm1% = Resistor [tolerance=±1% resistance=57 package=THT]
  J1 = female pin header, 4 pins [form="♀ (female)"]
  Arduino_MiniPro = Arduino Pro Mini v13
  J2 = female pin header, 4 pins [form="♀ (female)"]
  +5V = Header 2 [package=molex-1x2_lock]
  X_driver = EasyDriver_v44
  Y_driver = EasyDriver_v44

nets:
  N1: ULN2003A.In_1, Arduino_MiniPro.D13/SCK, Arduino_MiniPro.D12/MISO
  GND: ULN2003A.0V, 57ohm1%.Pin_1, Arduino_MiniPro.GND, +5V.1, X_driver.GND, Y_driver.GND
  VCC: ULN2003A.COM_-_Common, +5V_LSR.pin1, Arduino_MiniPro.VCC, +5V.2, X_driver.V+, X_driver.VCC, Y_driver.V+, Y_driver.VCC
  N2: ULN2003A.Out_1, +5V_LSR.pin2, 57ohm1%.Pin_0
  N3: J1.pin1, Y_driver.OUT1B
  N4: J1.pin2, Y_driver.OUT1A
  N5: J1.pin3, Y_driver.OUT2B
  N6: J1.pin4, Y_driver.OUT2A
  N7: Arduino_MiniPro.D8, X_driver.ENABLE, Y_driver.ENABLE
  N8: Arduino_MiniPro.D6_PWM, Y_driver.DIR
  N9: Arduino_MiniPro.D5_PWM, X_driver.DIR
  N10: Arduino_MiniPro.D3_PWM, Y_driver.STEP
  N11: Arduino_MiniPro.D2, X_driver.STEP
  N12: J2.pin1, X_driver.OUT1B
  N13: J2.pin2, X_driver.OUT1A
  N14: J2.pin3, X_driver.OUT2B
  N15: J2.pin4, X_driver.OUT2A

notes:
  GND
  +5V_IN
  laser_OUT
  +5V_laser
  DIR_X
  STEP_X
  Easy_driverV4.4
  axis_Y
  NEJE_300MW_DX8_ROSH_Laser_engraver Made with free software FRITZING
  Easy_driverV4.4
  axis_X
